# Fritzing sketch freemcom (saved by Fritzing 0.9.1b)
breadboards: 1

parts:
  arduino = Arduino Uno (Rev3)
  LED1_(for_12V) = LED - 5mm [color="Red (633nm)" package="5 mm [THT]"]
  J2 = Relay [part_number=SLD01101P package=THT]
  J1 = Relay [part_number=SLD01101P package=THT]
  XBee = XBee
  Reset = Pushbutton [package=THT]
  Start/Stop = Pushbutton [package=THT]
  R1 = Resistor [tolerance=±5% resistance=10k package=THT]
  Fuse1 = Fuse with Handler [part_number=10A]
  Buzzer(12V) = Piezo Speaker

nets:
  GND: arduino.GND, LED1_(for_12V).cathode, J2.COIL2, J1.COIL2, XBee.GND, Reset.leg0, R1.Pin_1, Buzzer(12V).pin2
  N1: arduino.D0/RX, XBee.pin2
  N2: arduino.D1/TX, XBee.pin3
  N3: arduino.D2, Start/Stop.leg0, R1.Pin_0
  N4: arduino.D6_PWM, J2.COIL1
  N5: arduino.D7, J1.COIL1
  N6: arduino.RESET, Reset.leg1
  3V3: arduino.3V3, XBee.VCC
  N7: arduino.5V, Start/Stop.leg1
  5V: arduino.VIN
  N8: LED1_(for_12V).anode, J2.C1, J2.C2
  N9: J2.A, J1.A, Fuse1.Connector2
  N10: J1.C1, J1.C2, Buzzer(12V).pin1
  12V: Fuse1.Connector1

notes:
  COM1
  NO1
  NO2
  COM2
